// Logisim project alu.circ as structural Verilog: 4 circuits, main circuit 4-bit ALU
module _1_bit_adder (
  input  CarryIn,
  input  a,
  input  b,
  output Sum,
  output CarryOut
);

  wire and_1_out, and_2_out, and_3_out;

  xor xor_1 (Sum, b, a, CarryIn);
  and and_1 (and_1_out, CarryIn, a);
  and and_2 (and_2_out, a, b);
  and and_3 (and_3_out, b, CarryIn);
  or or_1 (CarryOut, and_1_out, and_2_out, and_3_out);
endmodule

module _1_bit_ALU (
  input  CarryIn,
  input  Ainvert,
  input  a,
  input  [1:0] Operation,
  input  b,
  input  Binvert,
  input  Less,
  output Result,
  output CarryOut
);

  wire and_1_out, n1_bit_adder_1_sum, or_1_out, xor_1_out, xor_2_out;

  xor xor_1 (xor_1_out, Ainvert, a);
  xor xor_2 (xor_2_out, b, Binvert);
  _1_bit_adder u_1_bit_adder_1 (
    .CarryIn(CarryIn), .a(xor_1_out), .b(xor_2_out), .Sum(n1_bit_adder_1_sum), .CarryOut(CarryOut));
  and and_1 (and_1_out, xor_2_out, xor_1_out);
  or or_1 (or_1_out, xor_1_out, xor_2_out);
  Multiplexer #(.select(2)) multiplexer_1 (
    .in0(and_1_out), .in1(or_1_out), .in2(n1_bit_adder_1_sum), .in3(Less), .out(Result), .sel(Operation));
endmodule

module _4_bit_ALU (
  input  [3:0] ALU_operation,
  input  [3:0] a,
  input  [3:0] b,
  output Zero,
  output [3:0] Result,
  output Overflow,
  output CarryOUt
);

  wire n1_bit_alu_1_carryout, n1_bit_alu_2_carryout, n1_bit_alu_3_carryout, n1_bit_alu_last_1_lessthanzero;

  _1_bit_ALU u_1_bit_alu_1 (
    .Ainvert(ALU_operation[3]), .a(a[0]), .b(a[0]), .Binvert(ALU_operation[2]), .CarryIn(ALU_operation[3]),
    .CarryOut(n1_bit_alu_1_carryout), .Less(n1_bit_alu_last_1_lessthanzero), .Operation(ALU_operation[1:0]),
    .Result(Result[0]));
  _1_bit_ALU u_1_bit_alu_2 (
    .Ainvert(ALU_operation[3]), .a(a[1]), .b(b[1]), .Binvert(ALU_operation[2]),
    .CarryIn(n1_bit_alu_1_carryout), .CarryOut(n1_bit_alu_2_carryout), .Less(1'b0),
    .Operation(ALU_operation[1:0]), .Result(Result[1]));
  _1_bit_ALU u_1_bit_alu_3 (
    .Ainvert(ALU_operation[3]), .a(a[2]), .b(b[2]), .Binvert(ALU_operation[2]),
    .CarryIn(n1_bit_alu_2_carryout), .CarryOut(n1_bit_alu_3_carryout), .Less(1'b0),
    .Operation(ALU_operation[1:0]), .Result(Result[2]));
  _1_bit_ALU__last u_1_bit_alu_last_1 (
    .Ainvert(ALU_operation[3]), .a(a[3]), .b(b[3]), .Binvert(ALU_operation[2]),
    .CarryIn(n1_bit_alu_3_carryout), .CarryOut(CarryOUt), .Less(1'b0),
    .LessThanZero(n1_bit_alu_last_1_lessthanzero), .Operation(ALU_operation[1:0]), .Result(Result[3]),
    .Overflow(Overflow));
  nor nor_1 (Zero, Result[0], Result[1], Result[2], Result[3]);

  assign b[0] = a[0];
endmodule

module _1_bit_ALU__last (
  input  CarryIn,
  input  Ainvert,
  input  a,
  input  [1:0] Operation,
  input  b,
  input  Binvert,
  input  Less,
  output LessThanZero,
  output Result,
  output Overflow,
  output CarryOut
);

  wire and_1_out, n1_bit_adder_1_sum, or_1_out, xor_1_out, xor_2_out;

  xor xor_1 (xor_1_out, Ainvert, a);
  xor xor_2 (xor_2_out, b, Binvert);
  _1_bit_adder u_1_bit_adder_1 (
    .CarryIn(CarryIn), .a(xor_1_out), .b(xor_2_out), .Sum(n1_bit_adder_1_sum), .CarryOut(CarryOut));
  and and_1 (and_1_out, xor_2_out, xor_1_out);
  or or_1 (or_1_out, xor_1_out, xor_2_out);
  Multiplexer #(.select(2)) multiplexer_1 (
    .in0(and_1_out), .in1(or_1_out), .in2(n1_bit_adder_1_sum), .in3(Less), .out(Result), .sel(Operation));
  xor xor_3 (Overflow, CarryIn, CarryOut);
  xor xor_4 (LessThanZero, n1_bit_adder_1_sum, Overflow);
endmodule
